# Fritzing sketch Master Controller Setup (saved by Fritzing 0.9.1b)
breadboards: 1

parts:
  Part1 = Arduino Uno (Rev3)
  Raspberry_Pi1 = Raspberry Pi B+  # not connected
  Part2 = Arduino Leonardo (Rev3b)
  Part3 = Arduino Mega 2560 (Rev3)
  R1 = Resistor [tolerance=±5% resistance=4.7k package=THT]
  R2 = Resistor [tolerance=±5% resistance=4.7k package=THT]
  R3 = Resistor [tolerance=±5% resistance=4.7k package=THT]
  R4 = Resistor [tolerance=±5% resistance=4.7k package=THT]
  R5 = Resistor [tolerance=±5% resistance=4.7k package=THT]
  R6 = Resistor [tolerance=±5% resistance=4.7k package=THT]

nets:
  N1: Part1.A4/SDA, Part2.D2/SDA, Part2.SDA, Part3.D20/SDA, Part3.SDA, R1.Pin_1, R3.Pin_1, R6.Pin_1
  N2: Part1.A5/SCL, Part2.D3_PWM/SCL, Part2.SCL, Part3.D21/SCL, Part3.SCL, R2.Pin_1, R4.Pin_1, R5.Pin_1
  N3: Part1.5V, R1.Pin_0, R2.Pin_0
  N4: Part2.5V, R3.Pin_0, R4.Pin_0
  N5: Part3.5V, R5.Pin_0, R6.Pin_0

notes:
  Note: You do not have to hook up all the pins I have shown here on the arduinos. R3 Boards have a SDA and SCL pin breakout but earlier versions had them at different pin locations. It is easy to tell if you have a R3 board as it will have more pins than the older boards, after digital 13 there will be a Ground, AREF and then 2 more pins which is the SDA and SCL pins. They are labeled on the back of the uno R3 if you look. The arduino should use pull up resistors for both lines tied to 5V and should be between 4.7k - 10k resistors. Only the master needs pull-up resistors
  Meanwhile the Pi is pretty simple to hookup and no resistors are needed since there is already a 1.8K pullup on the SCL and SDA pins of the Pi. Make sure you are using 3.3v though, it should be ok as long as the Pi is the master but sending the Pi more than 3.3v can seriously damage it.
  The I2C spec calls for only 1 set of pullup resistors on the line but some devices may have thier own pullup resistors so you may need to change resistor values accordingly if you are expereincing problems.
