# Fritzing sketch ATTiny Moisture Sensor_led (saved by Fritzing 0.9.1b)
circuit board: 2.41054cm x 2.29089cm
perfboards: 1

parts:
  J3 = Screw terminal - 2 pins [package=THT]
  U1 = attiny85 [package=dip]
  LED1 = LED - 5mm [color="Red (633nm)" package="5 mm [THT]"]
  J1 = Screw terminal - 2 pins [package=THT]
  R1 = Resistor [tolerance=±5% resistance=220 package=THT]
  R2 = Resistor [tolerance=±5% resistance=68k package=THT]
  R3 = Resistor [tolerance=±5% resistance=100 package=THT]

nets:
  N1: J3.pin1, U1.Pin_2, R2.Pin_0
  N2: J3.pin2, R3.Pin_0
  N3: U1.Pin_3, R3.Pin_1
  N4: U1.Pin_4, J1.pin1, R1.Pin_0
  N5: U1.Pin_5, R2.Pin_1
  N6: U1.Pin_7, LED1.anode
  N7: U1.Pin_8, J1.pin2
  N8: LED1.cathode, R1.Pin_1

notes:
  Pin 2 = LED
  Pin 3 = Analog in
  pin 4 = Prong 2 100 ohm
  pin 0 = Prong 1 57-100k ohm
  Orange - is SCL for i2c
  White - is SDA for i2c
  Purple - is output for prongs
  Yellow - is LED Power
  Green - is the analog input for the moisture sensor

// code stored in the sketch: Tiny Moisture Sensor.ino
/* ATtiny85 as an I2C Slave            BroHogan                           1/12/11
 * Example of ATtiny I2C slave receiving and sending data to an Arduino master.
 * Gets data from master, adds 10 to it and sends it back.
 * SETUP:
 * ATtiny Pin 1 = (RESET) N/U                      ATtiny Pin 2 = (D3) N/U
 * ATtiny Pin 3 = (D4) to LED1                     ATtiny Pin 4 = GND
 * ATtiny Pin 5 = I2C SDA on DS1621  & GPIO        ATtiny Pin 6 = (D1) to LED2
 * ATtiny Pin 7 = I2C SCK on DS1621  & GPIO        ATtiny Pin 8 = VCC (2.7-5.5V)
 * NOTE! - It's very important to use pullups on the SDA & SCL lines!
 * Current Rx & Tx buffers set at 32 bytes - see usiTwiSlave.h
 * Credit and thanks to Don Blake for his usiTwiSlave code. 
 * More on TinyWireS usage - see TinyWireS.h
 */


#include "TinyWireS.h"                  // wrapper class for I2C slave routines

//this needs to change for each sensor
#define I2C_SLAVE_ADDR  0x01            // i2c slave address 

#define LED_PIN         1              // ATtiny Pin 6
#define MOISTURE_SENSOR	3

boolean isOn;
const int  MOISTURE_LEVEL = 250;

void setup(){
  pinMode(LED_PIN,OUTPUT);             // for general DEBUG use
	pinMode(MOISTURE_SENSOR, ANALOG);
  TinyWireS.begin(I2C_SLAVE_ADDR);      // init I2C Slave mode
}


void loop(){
	
	int reading = analogRead(MOISTURE_SENSOR);

	reading < MOISTURE_LEVEL ?  setLedState(true) : setLedState(false);

  byte byteRcvd = 0;
  if (TinyWireS.available()){           // got I2C input!
    byteRcvd = TinyWireS.receive();     // get the byte from master
    TinyWireS.send(isOn);           // send it back to master

  }
}

void setLedState(boolean state){
	if(isOn != state){
		isOn = state;
		isOn? digitalWrite(LED_PIN, HIGH) : digitalWrite(LED_PIN, LOW);
	}
}

}

// code stored in the sketch: Tiny_Moisture_Sensor_led.ino
#define POWER_PIN1      0              // ATtiny Pin 5
#define POWER_PIN2      4              // ATtiny Pin 3
#define LED_PIN         2              // ATtiny Pin 7
#define MOISTURE_SENSOR	3              // ATtiny Pin 2


//change this to your desired moisture level it may require some
//experimentation on your part to determine the optimal level
const int  MOISTURE_LEVEL = 250;

//our valriables and timer
int 	   val1, val2;
long       timer;

//check every 5 minutes 
const unsigned int DELAY_TIME = 300;

void setup(){
  timer = 0;

  pinMode(POWER_PIN1, OUTPUT);
  pinMode(POWER_PIN2, OUTPUT);
  pinMode(LED_PIN, OUTPUT);  
  pinMode(MOISTURE_SENSOR, INPUT);

  //here we do a quick setup and check. we dont want the sensor to corrode
  //so we will only be checking every once in awhile, also it is unlikely
  //that the soil will dry up in a matter of seconds or even minutes
  digitalWrite(POWER_PIN1, HIGH);
  digitalWrite(POWER_PIN2, LOW);
  val1 = analogRead(MOISTURE_SENSOR);
  delay(500);
  digitalWrite(POWER_PIN1, LOW);
  digitalWrite(POWER_PIN2, HIGH);
  val2 = 1023 - analogRead(MOISTURE_SENSOR);

  //turn things off 
  digitalWrite(POWER_PIN1, LOW);
  digitalWrite(POWER_PIN2, LOW);

  //set an inital state
  int avg = (val1 + val2) / 2;
  avg < MOISTURE_LEVEL ? digitalWrite(LED_PIN, HIGH) : digitalWrite(LED_PIN, LOW);
}

void readSensor(){

  digitalWrite(POWER_PIN1, HIGH);
  digitalWrite(POWER_PIN2, LOW);
  val1 = analogRead(MOISTURE_SENSOR);
  delay(500);
  digitalWrite(POWER_PIN1, LOW);
  digitalWrite(POWER_PIN2, HIGH);
  val2 = 1023 - analogRead(MOISTURE_SENSOR);

  //average things out
  int avg = (val1 + val2) / 2;

  //the more moist the soil the lower the resistance and thus higher the reading
  //a lower average means the soils dry
  avg < MOISTURE_LEVEL ? digitalWrite(LED_PIN, HIGH) : digitalWrite(LED_PIN, LOW);
}

void loop(){

  //only check when its time
  if(millis()-timer>1000*DELAY_TIME){
    readSensor();

    //set things back to low 
    digitalWrite(POWER_PIN1, LOW);
    digitalWrite(POWER_PIN2, LOW);

    //reset the timer
    timer = millis();
  }
}
